// Logisim project ping-pong.circ as structural Verilog: 4 circuits, main circuit movePoint
module movePoint (
);

  wire and_2_out, comp_y_cord_1_out_4, comp_y_cord_2_out_4, comparator_1_eq, comparator_2_eq,
       comparator_3_eq, comparator_4_eq, comparator_5_eq, counter_2_carry, d_ff_2_q, direction, isDown,
       makeNull, not_1_out, not_2_out, NULL_X, or_1_out, or_2_out, or_3_out, or_4_out, power, restart,
       swap_x_direction_left_wall, swap_x_direction_right_wall;
  wire [3:0] counter_2_q, counter_3_q, counter_4_q, hundr, hundr2, tens, tens2, units, units2;
  wire [4:0] xDirection;
  wire [6:0] keyboard;
  wire [7:0] counter_5_q, counter_6_q;
  wire [14:0] yDirection;
  wire [15:0] decoder_3_out0, demultiplexer_1_out1, demultiplexer_1_out2, demultiplexer_1_out3,
       demultiplexer_1_out4, demultiplexer_1_out5, demultiplexer_1_out6, demultiplexer_1_out7,
       demultiplexer_1_out8, demultiplexer_1_out9, demultiplexer_1_out10, demultiplexer_1_out11,
       demultiplexer_1_out12, demultiplexer_1_out13, demultiplexer_1_out14, demultiplexer_1_out15,
       demultiplexer_1_out16, demultiplexer_1_out17, demultiplexer_1_out18, demultiplexer_1_out19,
       demultiplexer_1_out20, demultiplexer_1_out21, demultiplexer_1_out22, demultiplexer_1_out23,
       demultiplexer_1_out24, demultiplexer_1_out25, demultiplexer_1_out26, demultiplexer_1_out27,
       demultiplexer_1_out28, plug, right_wall, rocket, rocket2, shifter_1_out, shifter_2_out, shifter_3_out,
       shifter_4_out, y_cord;

  Clock clock_1 (.out(power));
  Hex_Digit_Display hex_digit_display_1 (.value(hundr));  // open: dp
  Hex_Digit_Display hex_digit_display_2 (.value(tens));  // open: dp
  Counter #(.width(5), .max('h1f), .ongoal("load")) counter_1 (
    .load(d_ff_2_q), .Q(xDirection), .carry(NULL_X), .clk(power), .clr(or_1_out));  // open: D, count
  buf or_1 (or_1_out, restart);  // OR_Gate
  Hex_Digit_Display hex_digit_display_3 (.value(units));  // open: dp
  DotMatrix #(.matrixcols(32), .matrixrows(16)) dotmatrix_1 (
    .col0(rocket), .col1(y_cord), .col2(demultiplexer_1_out1), .col3(demultiplexer_1_out2),
    .col4(demultiplexer_1_out3), .col5(demultiplexer_1_out4), .col6(demultiplexer_1_out5),
    .col7(demultiplexer_1_out6), .col8(demultiplexer_1_out7), .col9(demultiplexer_1_out8),
    .col10(demultiplexer_1_out9), .col11(demultiplexer_1_out10), .col12(demultiplexer_1_out11),
    .col13(demultiplexer_1_out12), .col14(demultiplexer_1_out13), .col15(demultiplexer_1_out14),
    .col16(demultiplexer_1_out15), .col17(demultiplexer_1_out16), .col18(demultiplexer_1_out17),
    .col19(demultiplexer_1_out18), .col20(demultiplexer_1_out19), .col21(demultiplexer_1_out20),
    .col22(demultiplexer_1_out21), .col23(demultiplexer_1_out22), .col24(demultiplexer_1_out23),
    .col25(demultiplexer_1_out24), .col26(demultiplexer_1_out25), .col27(demultiplexer_1_out26),
    .col28(demultiplexer_1_out27), .col29(demultiplexer_1_out28), .col30(right_wall), .col31(rocket2));
  // Probe on xDirection
  D_Flip_Flop d_ff_1 (.Q(isDown), .preset(direction), .reset(and_2_out));  // open: clk, D, Qn, en
  not not_1 (not_1_out, swap_x_direction_left_wall);
  Comparator #(.width(5)) comparator_1 (.a(xDirection), .b({5{1'b0}}), .eq(comparator_1_eq));  // open: gt, lt
  Counter #(.width(4), .max('hf), .ongoal("load")) counter_2 (
    .load(isDown), .Q(counter_2_q), .carry(counter_2_carry), .clk(power), .clr(or_2_out));  // open: D, count
  buf or_2 (or_2_out, restart);  // OR_Gate
  not not_2 (not_2_out, not_2_out);
  Demultiplexer #(.select(5), .width(16)) demultiplexer_1 (
    .out0(y_cord), .out1(demultiplexer_1_out1), .out2(demultiplexer_1_out2), .out3(demultiplexer_1_out3),
    .out4(demultiplexer_1_out4), .out5(demultiplexer_1_out5), .out6(demultiplexer_1_out6),
    .out7(demultiplexer_1_out7), .out8(demultiplexer_1_out8), .out9(demultiplexer_1_out9),
    .out10(demultiplexer_1_out10), .out11(demultiplexer_1_out11), .out12(demultiplexer_1_out12),
    .out13(demultiplexer_1_out13), .out14(demultiplexer_1_out14), .out15(demultiplexer_1_out15),
    .out16(demultiplexer_1_out16), .out17(demultiplexer_1_out17), .out18(demultiplexer_1_out18),
    .out19(demultiplexer_1_out19), .out20(demultiplexer_1_out20), .out21(demultiplexer_1_out21),
    .out22(demultiplexer_1_out22), .out23(demultiplexer_1_out23), .out24(demultiplexer_1_out24),
    .out25(demultiplexer_1_out25), .out26(demultiplexer_1_out26), .out27(demultiplexer_1_out27),
    .out28(demultiplexer_1_out28), .out29(right_wall), .in({direction, yDirection}), .sel(xDirection));  // open: out30, out31, en
  Decoder #(.select(4)) decoder_1 (
    .out0(yDirection[0]), .out1(yDirection[1]), .out2(yDirection[2]), .out3(yDirection[3]),
    .out4(yDirection[4]), .out5(yDirection[5]), .out6(yDirection[6]), .out7(yDirection[7]),
    .out8(yDirection[8]), .out9(yDirection[9]), .out10(yDirection[10]), .out11(yDirection[11]),
    .out12(yDirection[12]), .out13(yDirection[13]), .out14(yDirection[14]), .out15(direction),
    .sel(counter_2_q));  // open: en
  and and_1 (makeNull, not_1_out, comparator_1_eq);
  D_Flip_Flop d_ff_2 (.Q(d_ff_2_q), .preset(swap_x_direction_right_wall), .reset(NULL_X));  // open: clk, D, Qn, en
  and and_2 (and_2_out, yDirection[0], counter_2_carry);
  Hex_Digit_Display hex_digit_display_4 (.value(hundr2));  // open: dp
  Hex_Digit_Display hex_digit_display_5 (.value(tens2));  // open: dp
  Keyboard #(.buflen(1)) keyboard_1 (.clk(power), .data(keyboard));  // open: re, clr, avail
  Hex_Digit_Display hex_digit_display_6 (.value(units2));  // open: dp
  Button button_1 (.out(restart));
  // Probe on keyboard
  // Probe on keyboard
  // Probe on keyboard
  // Probe on keyboard
  // Probe on rocket
  Comparator #(.width(7)) comparator_2 (.a(keyboard), .b(7'b1110111), .eq(comparator_2_eq));  // open: gt, lt
  Comparator #(.width(7)) comparator_3 (.a(keyboard), .b(7'b1110011), .eq(comparator_3_eq));  // open: gt, lt
  Comparator #(.width(7)) comparator_4 (.a(keyboard), .b(7'b1101111), .eq(comparator_4_eq));  // open: gt, lt
  Comparator #(.width(7)) comparator_5 (.a(keyboard), .b(7'b1101100), .eq(comparator_5_eq));  // open: gt, lt
  // Probe on rocket2
  or or_3 (or_3_out, comparator_2_eq, comparator_3_eq);
  or or_4 (or_4_out, comparator_4_eq, comparator_5_eq);
  Counter #(.width(4), .max('hf)) counter_3 (
    .load(comparator_3_eq), .Q(counter_3_q), .clk(or_3_out));  // open: D, count, carry, clr
  Counter #(.width(4), .max('hf)) counter_4 (
    .load(comparator_5_eq), .Q(counter_4_q), .clk(or_4_out));  // open: D, count, carry, clr
  comp_y_cord comp_y_cord_1 (.in_1(rocket2), .in_2(right_wall), .in_3(isDown), .out_4(comp_y_cord_1_out_4));
  comp_y_cord comp_y_cord_2 (.in_1(rocket), .in_2(y_cord), .in_3(isDown), .out_4(comp_y_cord_2_out_4));
  Decoder #(.select(4)) decoder_2 (
    .out0(plug[0]), .out1(plug[1]), .out2(plug[2]), .out3(plug[3]), .out4(plug[4]), .out5(plug[5]),
    .out6(plug[6]), .out7(plug[7]), .out8(plug[8]), .out9(plug[9]), .out10(plug[10]), .out11(plug[11]),
    .out12(plug[12]), .out13(plug[13]), .out14(plug[14]), .out15(plug[15]), .sel(counter_3_q));  // open: en
  Decoder #(.select(4)) decoder_3 (
    .out0(decoder_3_out0[0]), .out1(decoder_3_out0[1]), .out2(decoder_3_out0[2]), .out3(decoder_3_out0[3]),
    .out4(decoder_3_out0[4]), .out5(decoder_3_out0[5]), .out6(decoder_3_out0[6]), .out7(decoder_3_out0[7]),
    .out8(decoder_3_out0[8]), .out9(decoder_3_out0[9]), .out10(decoder_3_out0[10]),
    .out11(decoder_3_out0[11]), .out12(decoder_3_out0[12]), .out13(decoder_3_out0[13]),
    .out14(decoder_3_out0[14]), .out15(decoder_3_out0[15]), .sel(counter_4_q));  // open: en
  Comparator #(.width(1)) comparator_6 (
    .a(comp_y_cord_1_out_4), .b(1'b1), .eq(swap_x_direction_right_wall));  // open: gt, lt
  Comparator #(.width(1)) comparator_7 (
    .a(comp_y_cord_2_out_4), .b(1'b1), .eq(swap_x_direction_left_wall));  // open: gt, lt
  Counter #(.ongoal("continue")) counter_5 (
    .Q(counter_5_q), .clk(swap_x_direction_right_wall), .clr(restart));  // open: load, D, count, carry
  Counter #(.ongoal("continue")) counter_6 (
    .Q(counter_6_q), .clk(swap_x_direction_left_wall), .clr(restart));  // open: load, D, count, carry
  Shifter #(.width(16)) shifter_1 (.in(plug), .\dist (4'b0001), .out(shifter_1_out));
  Shifter #(.width(16), .shift("lr")) shifter_2 (.in(plug), .\dist (4'b0001), .out(shifter_2_out));
  Shifter #(.width(16)) shifter_3 (.in(decoder_3_out0), .\dist (4'b0001), .out(shifter_3_out));
  Shifter #(.width(16), .shift("lr")) shifter_4 (.in(decoder_3_out0), .\dist (4'b0001), .out(shifter_4_out));
  parseScore parsescore_1 (.in_1(counter_5_q), .out_2(hundr2), .out_3(tens2), .out_4(units2));
  parseScore parsescore_2 (.in_1(counter_6_q), .out_2(hundr), .out_3(tens), .out_4(units));
  assign rocket = shifter_1_out | plug | shifter_2_out;  // OR_Gate or_5, 16 bits wide
  assign rocket2 = shifter_3_out | decoder_3_out0 | shifter_4_out;  // OR_Gate or_6, 16 bits wide

  // Other names for the same wires on the sheet: yDirection[15] = direction

  // Notes on the sheet:
  //   SCORE
  //   Player 1
  //   не работает(прекращение работы)
  //   отскок от правой стенки
  //   выход на 0 на счетчиках
  //   Inputs
  //   SCORE
  //   Player 2
  //   w, s // o, l
  //   PLAYER_1
  //   PLAYER_2
  //   в будущем ии
  //   Keyboard input
  //   Keyboard input
  //   если попадание: правая стенка
  //   если попадание: левая стенка
endmodule

// ||
module comp_y_cord (
  input  [15:0] in_1,
  input  [15:0] in_2,
  input  in_3,
  output out_4
);

  wire and_1_out, and_2_out, and_3_out, and_4_out, and_5_out, and_6_out, and_7_out, and_8_out, and_9_out,
       and_10_out, and_11_out, and_12_out, and_13_out, and_14_out, and_15_out, and_16_out, and_17_out,
       and_18_out, and_19_out, and_20_out, and_21_out, and_22_out, and_23_out, and_24_out, and_25_out,
       and_26_out, and_27_out, and_28_out, and_29_out, and_30_out, and_31_out, and_32_out, and_33_out,
       and_34_out, and_35_out, and_36_out, and_37_out, and_38_out, and_39_out, and_40_out, and_41_out,
       and_42_out, and_43_out, and_44_out, or_1_out, or_2_out, or_3_out, or_4_out, or_5_out, or_6_out,
       or_7_out, or_8_out, or_9_out, or_10_out, or_11_out, or_12_out, or_13_out, or_14_out, or_15_out,
       or_16_out, or_17_out, or_18_out, or_19_out, or_20_out, or_21_out, or_22_out, or_23_out, or_24_out,
       or_25_out, or_26_out, or_27_out, or_28_out, or_30_out, or_31_out, or_32_out, or_33_out, undriven;

  or or_1 (or_1_out, in_1[0], in_1[1]);
  or or_2 (or_2_out, in_1[0], in_1[1], in_1[2]);
  or or_3 (or_3_out, in_1[1], in_1[2], in_1[3]);
  or or_4 (or_4_out, in_1[2], in_1[3], in_1[4]);
  or or_5 (or_5_out, in_1[3], in_1[4], in_1[5]);
  or or_6 (or_6_out, in_1[4], in_1[5], in_1[6]);
  or or_7 (or_7_out, in_1[5], in_1[6], in_1[7]);
  or or_8 (or_8_out, in_1[6], in_1[7], in_1[8]);
  or or_9 (or_9_out, in_1[7], in_1[8], in_1[9]);
  or or_10 (or_10_out, in_1[8], in_1[9], in_1[10]);
  or or_11 (or_11_out, in_1[9], in_1[10], in_1[11]);
  or or_12 (or_12_out, in_1[10], in_1[11], in_1[12]);
  or or_13 (or_13_out, in_1[11], in_1[12], in_1[13]);
  or or_14 (or_14_out, in_1[12], in_1[13], in_1[14]);
  or or_15 (or_15_out, in_1[1], in_1[2], in_1[3]);
  or or_16 (or_16_out, in_1[2], in_1[3], in_1[4]);
  or or_17 (or_17_out, in_1[3], in_1[4], in_1[5]);
  or or_18 (or_18_out, in_1[4], in_1[5], in_1[6]);
  or or_19 (or_19_out, in_1[5], in_1[6], in_1[7]);
  or or_20 (or_20_out, in_1[6], in_1[7], in_1[8]);
  or or_21 (or_21_out, in_1[7], in_1[8], in_1[9]);
  or or_22 (or_22_out, in_1[8], in_1[9], in_1[10]);
  or or_23 (or_23_out, in_1[9], in_1[10], in_1[11]);
  or or_24 (or_24_out, in_1[10], in_1[11], in_1[12]);
  or or_25 (or_25_out, in_1[11], in_1[12], in_1[13]);
  or or_26 (or_26_out, in_1[12], in_1[13], in_1[14]);
  or or_27 (or_27_out, in_1[13], in_1[14], in_1[15]);
  or or_28 (or_28_out, in_1[14], in_1[15]);
  and and_1 (and_1_out, in_1[0], in_2[0]);
  and and_2 (and_2_out, in_1[1], in_2[1]);
  and and_3 (and_3_out, in_1[2], in_2[2]);
  and and_4 (and_4_out, in_1[3], in_2[3]);
  and and_5 (and_5_out, in_1[4], in_2[4]);
  and and_6 (and_6_out, in_1[5], in_2[5]);
  and and_7 (and_7_out, in_1[6], in_2[6]);
  and and_8 (and_8_out, in_1[7], in_2[7]);
  and and_9 (and_9_out, in_1[8], in_2[8]);
  and and_10 (and_10_out, in_1[9], in_2[9]);
  and and_11 (and_11_out, in_1[10], in_2[10]);
  and and_12 (and_12_out, in_1[11], in_2[11]);
  and and_13 (and_13_out, in_1[12], in_2[12]);
  and and_14 (and_14_out, in_1[13], in_2[13]);
  and and_15 (and_15_out, in_1[14], in_2[14]);
  and and_16 (and_16_out, in_1[15], in_2[15]);
  and and_17 (and_17_out, or_1_out, in_2[2]);
  and and_18 (and_18_out, or_2_out, in_2[3]);
  and and_19 (and_19_out, or_3_out, in_2[4]);
  and and_20 (and_20_out, or_4_out, in_2[5]);
  and and_21 (and_21_out, or_5_out, in_2[6]);
  and and_22 (and_22_out, or_6_out, in_2[7]);
  and and_23 (and_23_out, or_7_out, in_2[8]);
  and and_24 (and_24_out, or_8_out, in_2[9]);
  and and_25 (and_25_out, or_9_out, in_2[10]);
  and and_26 (and_26_out, or_10_out, in_2[11]);
  and and_27 (and_27_out, or_11_out, in_2[12]);
  and and_28 (and_28_out, or_12_out, in_2[13]);
  and and_29 (and_29_out, or_13_out, in_2[14]);
  and and_30 (and_30_out, or_14_out, in_2[15]);
  and and_31 (and_31_out, in_2[0], or_15_out);
  and and_32 (and_32_out, in_2[1], or_16_out);
  and and_33 (and_33_out, in_2[2], or_17_out);
  and and_34 (and_34_out, in_2[3], or_18_out);
  and and_35 (and_35_out, in_2[4], or_19_out);
  and and_36 (and_36_out, in_2[5], or_20_out);
  and and_37 (and_37_out, in_2[6], or_21_out);
  and and_38 (and_38_out, in_2[7], or_22_out);
  and and_39 (and_39_out, in_2[8], or_23_out);
  and and_40 (and_40_out, in_2[9], or_24_out);
  and and_41 (and_41_out, in_2[10], or_25_out);
  and and_42 (and_42_out, in_2[11], or_26_out);
  and and_43 (and_43_out, in_2[12], or_27_out);
  and and_44 (and_44_out, in_2[13], or_28_out);
  or or_29 (out_4, and_1_out, and_2_out, and_3_out, and_4_out, and_5_out, and_6_out, and_7_out, and_8_out, and_9_out, and_10_out, and_11_out, and_12_out, and_13_out, and_14_out, and_15_out, and_16_out);
  or or_30 (or_30_out, and_17_out, and_18_out, and_19_out, and_20_out, and_21_out, and_22_out, and_23_out, and_24_out, and_25_out, and_26_out, and_27_out, and_28_out, and_29_out, and_30_out);
  or or_31 (or_31_out, and_31_out, and_32_out, and_33_out, and_34_out, and_35_out, and_36_out, and_37_out, and_38_out, and_39_out, and_40_out, and_41_out, and_42_out, and_43_out, and_44_out);
  or or_32 (or_32_out, undriven, or_30_out);
  or or_33 (or_33_out, undriven, or_31_out);
  Multiplexer multiplexer_1 (.in0(or_33_out), .in1(or_32_out), .sel(in_3));  // open: out, en

  // Other names for the same wires on the sheet: _1_down = in_3; _0 = in_2[0]; ball_cord_y[15:0] = in_2; _1 = in_2[1];
  //   _2 = in_2[2]; _3 = in_2[3]; _4 = in_2[4]; _5 = in_2[5]; _6 = in_2[6]; _7 = in_2[7]; _8 = in_2[8]; _9 = in_2[9];
  //   _10 = in_2[10]; _11 = in_2[11]; _12 = in_2[12]; _13 = in_2[13]; _14 = in_2[14]; _15 = in_2[15];
  //   rock_cord_y[15:0] = in_1

  // Notes on the sheet:
  //   ракетка
  //   шарик
  //   сверху вниз
  //   0,1|2
  //   0,1,2|3
  //   1,2,3|4
  //   2,3,4|5
  //   3,4,5|6
  //   4,5,6|7
  //   5,6,7|8
  //   6,7,8|9
  //   7,8,9|10
  //   9,10,11|12
  //   6,7,8|5
  //   7,8,9|6
  //   8,9,10|7
  //   8,9,10|11
  //   10,11,12|13
  //   11,12,13|14
  //   10,11,12|9
  //   11,12,13|10
  //   12,13,14|11
endmodule

module parseScore (
  input  [7:0] in_1,
  output [3:0] out_2,
  output [3:0] out_3,
  output [3:0] out_4
);

  wire [7:0] divider_1_out, divider_2_out, multiplier_1_out, multiplier_2_out, subtractor_1_out,
       subtractor_2_out;

  // Probe on in_1
  // Probe on divider_1_out
  Divider divider_1 (.a(in_1), .b(8'ha), .out(divider_1_out));  // open: upper, rem
  Divider divider_2 (.a(divider_1_out), .b(8'ha), .out(divider_2_out));  // open: upper, rem
  Multiplier multiplier_1 (.a(divider_1_out), .b(8'ha), .out(multiplier_1_out));  // open: cin, cout
  // Probe on multiplier_1_out
  // Probe on multiplier_2_out
  Multiplier multiplier_2 (.a(divider_2_out), .b(8'ha), .out(multiplier_2_out));  // open: cin, cout
  Bit_Extender #(.out_width(4)) bit_extender_1 (.in(divider_2_out), .out(out_2));
  Subtractor subtractor_1 (.a(in_1), .b(multiplier_1_out), .out(subtractor_1_out));  // open: bin, bout
  // Probe on out_2
  // Probe on subtractor_2_out
  Subtractor subtractor_2 (.a(divider_1_out), .b(multiplier_2_out), .out(subtractor_2_out));  // open: bin, bout
  // Probe on subtractor_1_out
  Bit_Extender #(.out_width(4)) bit_extender_2 (.in(subtractor_2_out), .out(out_3));
  Bit_Extender #(.out_width(4)) bit_extender_3 (.in(subtractor_1_out), .out(out_4));
endmodule

module ai_right_rocket (
  input  [15:0] in_1,
  input  [15:0] in_2
);


  // Notes on the sheet:
  //   y_cord_of_ball
  //   y_cord_of_rocket
endmodule
